// Logisim project Tic-Tac-Toe.circ as structural Verilog: 1 circuit, main circuit main
module main (
);

  wire and_2_out, and_3_out, and_4_out, and_5_out, and_6_out, B1, B2, B3, B4, B5, B6, B7, B8, B9, cl, code,
       I_Osel, in_out, mem, nor_1_out, nor_2_out, not_1_out, not_2_out, not_3_out, not_5_out, not_6_out,
       rs_latch_1_q_prime, RST, transistor_1_out, win_loose_screen_1_computer, win_loose_screen_1_draw,
       win_loose_screen_1_player;
  wire [1:0] CurrInput;
  wire [2:0] PageNum;
  wire [3:0] controlled_buffer_2_out, pull_resistor_3_node, register_1_q, S1, S2, S3, S4, S5, S6, S7, S8, S9;
  wire [7:0] addr, Cdm8_in, Cdm8_out, cdm_8_1_pc, cdm_8_1_ps, cdm_8_1_r0, cdm_8_1_r1, cdm_8_1_r2, cdm_8_1_r3,
       cdm_8_1_sp, codeData, I_Odat, move_selector_1_move, rom_1_data, rom_2_data, rom_3_data;
  wire [7:7] not_4_out;
  wire [30:0] display_controller_1_col0, display_controller_1_col1, display_controller_1_col2,
       display_controller_1_col3, display_controller_1_col4, display_controller_1_col5,
       display_controller_1_col6, display_controller_1_col7, display_controller_1_col8,
       display_controller_1_col9, display_controller_1_col10, display_controller_1_col11,
       display_controller_1_col12, display_controller_1_col13, display_controller_1_col14,
       display_controller_1_col15, display_controller_1_col16, display_controller_1_col17,
       display_controller_1_col18, display_controller_1_col19, display_controller_1_col20,
       display_controller_1_col21, display_controller_1_col22, display_controller_1_col23,
       display_controller_1_col24, display_controller_1_col25, display_controller_1_col26,
       display_controller_1_col27, display_controller_1_col28, display_controller_1_col29,
       display_controller_1_col30;

  // Probe on cdm_8_1_r0
  Clock clock_1 (.out(cl));
  Pull_Resistor pull_resistor_1 (.node(I_Odat));
  and and_1 (CurrInput[1], addr[4], addr[5], addr[6], addr[7]);
  DotMatrix #(.matrixcols(31), .matrixrows(31)) dotmatrix_1 (
    .col0(display_controller_1_col0), .col1(display_controller_1_col1), .col2(display_controller_1_col2),
    .col3(display_controller_1_col3), .col4(display_controller_1_col4), .col5(display_controller_1_col5),
    .col6(display_controller_1_col6), .col7(display_controller_1_col7), .col8(display_controller_1_col8),
    .col9(display_controller_1_col9), .col10(display_controller_1_col10), .col11(display_controller_1_col11),
    .col12(display_controller_1_col12), .col13(display_controller_1_col13),
    .col14(display_controller_1_col14), .col15(display_controller_1_col15),
    .col16(display_controller_1_col16), .col17(display_controller_1_col17),
    .col18(display_controller_1_col18), .col19(display_controller_1_col19),
    .col20(display_controller_1_col20), .col21(display_controller_1_col21),
    .col22(display_controller_1_col22), .col23(display_controller_1_col23),
    .col24(display_controller_1_col24), .col25(display_controller_1_col25),
    .col26(display_controller_1_col26), .col27(display_controller_1_col27),
    .col28(display_controller_1_col28), .col29(display_controller_1_col29), .col30(display_controller_1_col30));
  Display_controller display_controller_1 (
    .S1(S1), .S2(S2), .S3(S3), .S4(S4), .S5(S5), .S6(S6), .S7(S7), .S8(S8), .S9(S9),
    .Col0(display_controller_1_col0), .Col10(display_controller_1_col10), .Col20(display_controller_1_col20),
    .Col1(display_controller_1_col1), .Col11(display_controller_1_col11), .Col21(display_controller_1_col21),
    .Col2(display_controller_1_col2), .Col12(display_controller_1_col12), .Col22(display_controller_1_col22),
    .Col3(display_controller_1_col3), .Col13(display_controller_1_col13), .Col23(display_controller_1_col23),
    .Col4(display_controller_1_col4), .Col14(display_controller_1_col14), .Col24(display_controller_1_col24),
    .Col5(display_controller_1_col5), .Col15(display_controller_1_col15), .Col25(display_controller_1_col25),
    .Col6(display_controller_1_col6), .Col16(display_controller_1_col16), .Col26(display_controller_1_col26),
    .Col7(display_controller_1_col7), .Col17(display_controller_1_col17), .Col27(display_controller_1_col27),
    .Col8(display_controller_1_col8), .Col18(display_controller_1_col18), .Col28(display_controller_1_col28),
    .Col9(display_controller_1_col9), .Col19(display_controller_1_col19), .Col29(display_controller_1_col29),
    .Col30(display_controller_1_col30));
  // Probe on cdm_8_1_r2
  // Probe on cdm_8_1_r3
  // Probe on cdm_8_1_r1
  // Probe on cdm_8_1_pc
  Demultiplexer #(.width(8)) demultiplexer_1 (
    .out1(I_Odat), .in(Cdm8_out), .sel(CurrInput[1]), .en(and_2_out));  // open: out0
  and and_2 (and_2_out, ~in_out, mem);  // AND_Gate
  // Probe on cdm_8_1_ps
  // Probe on cdm_8_1_sp
  Pull_Resistor pull_resistor_2 (.node(addr));
  Decoder #(.select(2), .disabled(0)) decoder_1 (
    .out0(code), .out3(I_Osel), .sel(CurrInput), .en(mem));  // open: out1, out2
  CdM_8 cdm_8_1 (
    .data_code_prime(CurrInput[0]), .R0(cdm_8_1_r0), .R1(cdm_8_1_r1), .mem(mem), .R2(cdm_8_1_r2),
    .load_st_prime(in_out), .R3(cdm_8_1_r3), .addr(addr), .PC(cdm_8_1_pc), .SP(cdm_8_1_sp),
    .data_out(Cdm8_out), .data_in(Cdm8_in), .page(PageNum), .PS(cdm_8_1_ps), .clk(cl), .rset(RST));  // open: IAck, IRQ, vector, shadow
  Multiplexer #(.width(8)) multiplexer_1 (
    .in0(codeData), .in1(I_Odat), .out(Cdm8_in), .sel(CurrInput[1]), .en(and_3_out));
  and and_3 (and_3_out, in_out, mem);
  PS_saver ps_saver_1 (.I_Odat(I_Odat), .out(I_Odat), .in_out(in_out), .I_O_Adr(addr[3:0]), .I_O_sel(I_Osel));
  SP_saver sp_saver_1 (.I_Odat(I_Odat), .out(I_Odat), .in_out(in_out), .I_O_Adr(addr[3:0]), .I_O_sel(I_Osel));
  LED Draw (.in(win_loose_screen_1_draw));
  LED Player (.in(win_loose_screen_1_player));
  Win_loose_screen win_loose_screen_1 (
    .I_Odat(I_Odat), .player(win_loose_screen_1_player), .computer(win_loose_screen_1_computer),
    .in_out(in_out), .I_O_Adr(addr[3:0]), .I_O_sel(I_Osel), .Draw(win_loose_screen_1_draw), .I_Odat_2(I_Odat));
  Button button_1 (.out(B1));
  Button button_2 (.out(B2));
  Button button_3 (.out(B4));
  Button button_4 (.out(B5));
  Button button_5 (.out(B8));
  Button button_6 (.out(B7));
  LED Computer (.in(win_loose_screen_1_computer));
  Button button_7 (.out(B3));
  Button button_8 (.out(B6));
  Button button_9 (.out(B9));
  ROM rom_1 (.addr(addr), .data(rom_1_data), .sel(code));
  ROM rom_2 (.addr(addr), .data(rom_2_data), .sel(code));
  ROM rom_3 (.addr(addr), .data(rom_3_data), .sel(code));
  Button Restart (.out(RST));
  Multiplexer #(.select(2), .width(8), .disabled(0), .enable("false")) multiplexer_2 (
    .in0(rom_1_data), .in1(rom_2_data), .in2(rom_3_data), .out(codeData), .sel(PageNum[1:0]));  // open: in3
  DisplayReg1 displayreg1_1 (
    .in_out(in_out), .I_Odat(I_Odat[3:0]), .value(S1), .I_Oadr(addr[3:0]), .I_Osel(I_Osel), .out(I_Odat[3:0]));
  DisplayReg2 displayreg2_1 (
    .in_out(in_out), .I_Odat(I_Odat[3:0]), .value(S2), .I_Oadr(addr[3:0]), .I_Osel(I_Osel), .out(I_Odat[3:0]));
  Move_Selector move_selector_1 (
    .S1(S1), .S2(S2), .S3(S3), .S4(S4), .S5(S5), .S6(S6), .S7(S7), .S8(S8), .S9(S9),
    .Move(move_selector_1_move), .CL(cl));
  and and_4 (and_4_out, I_Osel, addr[0], addr[1], ~addr[2], addr[3], in_out);  // AND_Gate
  DisplayReg3 displayreg3_1 (
    .in_out(in_out), .I_Odat(I_Odat[3:0]), .value(S3), .I_Oadr(addr[3:0]), .I_Osel(I_Osel), .out(I_Odat[3:0]));
  assign I_Odat = and_4_out ? move_selector_1_move : 8'bz;  // Controlled_Buffer controlled_buffer_1
  DisplayReg4 displayreg4_1 (
    .in_out(in_out), .I_Odat(I_Odat[3:0]), .value(S4), .I_Oadr(addr[3:0]), .I_Osel(I_Osel), .out(I_Odat[3:0]));
  not not_1 (not_1_out, transistor_1_out);
  DisplayReg5 displayreg5_1 (
    .in_out(in_out), .I_Odat(I_Odat[3:0]), .value(S5), .I_Oadr(addr[3:0]), .I_Osel(I_Osel), .out(I_Odat[3:0]));
  DisplayReg6 displayreg6_1 (
    .in_out(in_out), .I_Odat(I_Odat[3:0]), .value(S6), .I_Oadr(addr[3:0]), .I_Osel(I_Osel), .out(I_Odat[3:0]));
  Transistor #(.\type ("n")) transistor_1 (.in(1'b0), .out(transistor_1_out), .gate(B1));
  assign controlled_buffer_2_out = B1 ? 4'b0001 : 4'bz;  // Controlled_Buffer controlled_buffer_2
  DisplayReg7 displayreg7_1 (
    .in_out(in_out), .I_Odat(I_Odat[3:0]), .value(S7), .I_Oadr(addr[3:0]), .I_Osel(I_Osel), .out(I_Odat[3:0]));
  Transistor #(.\type ("n")) transistor_2 (.in(1'b0), .out(transistor_1_out), .gate(B2));
  Transistor #(.\type ("n")) transistor_3 (.in(1'b0), .out(transistor_1_out), .gate(B3));
  assign controlled_buffer_2_out = B2 ? 4'b0010 : 4'bz;  // Controlled_Buffer controlled_buffer_3
  assign controlled_buffer_2_out = B3 ? 4'b0011 : 4'bz;  // Controlled_Buffer controlled_buffer_4
  not not_2 (not_2_out, not_1_out);
  not not_3 (not_3_out, and_6_out);
  DisplayReg8 displayreg8_1 (
    .in_out(in_out), .I_Odat(I_Odat[3:0]), .value(S8), .I_Oadr(addr[3:0]), .I_Osel(I_Osel), .out(I_Odat[3:0]));
  Transistor #(.\type ("n")) transistor_4 (.in(1'b0), .out(transistor_1_out), .gate(B4));
  Transistor #(.\type ("n")) transistor_5 (.in(1'b0), .out(transistor_1_out), .gate(B5));
  assign controlled_buffer_2_out = B5 ? 4'b0101 : 4'bz;  // Controlled_Buffer controlled_buffer_5
  assign controlled_buffer_2_out = B4 ? 4'b0100 : 4'bz;  // Controlled_Buffer controlled_buffer_6
  nor nor_1 (nor_1_out, not_1_out, not_2_out);
  nor nor_2 (nor_2_out, and_6_out, not_3_out);
  Pull_Resistor pull_resistor_3 (.node(pull_resistor_3_node));
  DisplayReg9 displayreg9_1 (
    .in_out(in_out), .I_Odat(I_Odat[3:0]), .value(S9), .I_Oadr(addr[3:0]), .I_Osel(I_Osel), .out(I_Odat[3:0]));
  Transistor #(.\type ("n")) transistor_6 (.in(1'b0), .out(transistor_1_out), .gate(B7));
  Transistor #(.\type ("n")) transistor_7 (.in(1'b0), .out(transistor_1_out), .gate(B6));
  assign controlled_buffer_2_out = B6 ? 4'b0110 : 4'bz;  // Controlled_Buffer controlled_buffer_7
  assign controlled_buffer_2_out = B7 ? 4'b0111 : 4'bz;  // Controlled_Buffer controlled_buffer_8
  RS_latch rs_latch_1 (.S(nor_1_out), .R(nor_2_out), .Q_prime(rs_latch_1_q_prime));  // open: Q, reset
  not not_4 (not_4_out[7], rs_latch_1_q_prime);
  Pull_Resistor #(.pull(1)) pull_resistor_4 (.node(transistor_1_out));
  Transistor #(.\type ("n")) transistor_8 (.in(1'b0), .out(transistor_1_out), .gate(B8));
  Transistor #(.\type ("n")) transistor_9 (.in(1'b0), .out(transistor_1_out), .gate(B9));
  assign controlled_buffer_2_out = B9 ? 4'b1001 : 4'bz;  // Controlled_Buffer controlled_buffer_9
  assign controlled_buffer_2_out = B8 ? 4'b1000 : 4'bz;  // Controlled_Buffer controlled_buffer_10
  not not_5 (not_5_out, transistor_1_out);
  not not_6 (not_6_out, not_5_out);
  Register #(.width(4), .trigger("falling")) register_1 (
    .D(controlled_buffer_2_out), .Q(register_1_q), .clk(not_6_out));  // open: en, clr
  assign I_Odat = and_6_out ? {{4{not_4_out[7]}}, register_1_q} : 8'bz;  // Controlled_Buffer controlled_buffer_11
  and and_5 (and_5_out, ~addr[0], addr[1], ~addr[2], addr[3], I_Osel);  // AND_Gate
  and and_6 (and_6_out, and_5_out, in_out);

  // Other names for the same wires on the sheet: I_OData[7:0] = I_Odat; I_Oadr[3:0] = addr[3:0];
  //   I_OSet = CurrInput[1]; rd_rw = in_out

  // Notes on the sheet:
  //   ROM0 (main program)
  //   ROM1 (X-Win arbiter)
  //   ROM2 (0-Win arbiter)
  //   contents of rom_1 (hex, n*v repeats v):
  //   d0 f0 d1 ff 8c a2 74 ec 4 d0 fa b1 5 e5 b b7 f e1 9 d2 3 a6 db 10 d0 fb b2 d3 f9 7e e4 18 d3 f0 7e
  //   e0 18 bb f e1 18 d3 2 ab db 20 ee 9 d4
  //   contents of rom_2 (hex, n*v repeats v):
  //   d0 f1 b1 d2 3 d3 30 79 e1 40 d0 f2 b1 79 e1 1c d0 f3 b1 79 e1 1c d0 fc a2 d0 ff a3 d0 f4 b1 79 e1 2e
  //   d0 f7 b1 79 e1 2e d0 fc a2 d0 ff a3 d0 f5 b1 79 e1 40 d0 f9 b1 79 e1 40 d0 fc a2 d0 ff a3 d0 f5 b1
  //   79 e1 7c d0 f3 b1 79 e1 58 d0 f7 b1 79 e1 58 d0 fc a2 d0 ff a3 d0 f2 b1 79 e1 6a d0 f8 b1 79 e1 6a
  //   d0 fc a2 d0 ff a3 d0 f4 b1 79 e1 7c d0 f6 b1 79 e1 7c d0 fc a2 d0 ff a3 d0 f9 b1 79 e1 a6 d0 f3 b1
  //   79 e1 94 d0 f6 b1 79 e1 94 d0 fc a2 d0 ff a3 d0 f7 b1 79 e1 a6 d0 f8 b1 79 e1 a6 d0 fc a2 d0 ff a3
  //   d0 f1 b1 5 ed e0 8c b1 5 ed e0 8c b1 5 ed e0 8c b1 5 ed e0 8c b1 5 ed e0 8c b1 5 ed e0 8c b1 5 ed e0
  //   8c b1 5 ed e0 8c b1 5 ed e0 d0 fc b1 5 e1 e0 d2 1 a2 d0 ff a3 d9
  //   contents of rom_3 (hex, n*v repeats v):
  //   d0 f1 b1 d2 2 d3 30 79 e1 40 d0 f2 b1 79 e1 1c d0 f3 b1 79 e1 1c d0 fc a2 d0 ff a3 d0 f4 b1 79 e1 2e
  //   d0 f7 b1 79 e1 2e d0 fc a2 d0 ff a3 d0 f5 b1 79 e1 40 d0 f9 b1 79 e1 40 d0 fc a2 d0 ff a3 d0 f5 b1
  //   79 e1 7c d0 f3 b1 79 e1 58 d0 f7 b1 79 e1 58 d0 fc a2 d0 ff a3 d0 f2 b1 79 e1 6a d0 f8 b1 79 e1 6a
  //   d0 fc a2 d0 ff a3 d0 f4 b1 79 e1 7c d0 f6 b1 79 e1 7c d0 fc a2 d0 ff a3 d0 f9 b1 79 e1 a6 d0 f3 b1
  //   79 e1 94 d0 f6 b1 79 e1 94 d0 fc a2 d0 ff a3 d0 f7 b1 79 e1 a6 d0 f8 b1 79 e1 a6 d0 fc a2 d0 ff a3
  //   d9
  //   I/O Adr: 11111011
  //   Input controller
  //   I/O Adr: 11111010
  //   Screen choosers
endmodule
