// Logisim project Tic-Tac-Toe_Modules.circ as structural Verilog: 14 circuits, main circuit DisplayReg1
module DisplayControl (
  input  [3:0] \input ,
  output [17:0] outSignals_1_2,
  output [26:0] outSignals_3_4_5
);

  Multiplexer #(.width(18), .disabled(0)) multiplexer_1 (
    .in0(18'h202fe), .in1(18'h10501), .out(outSignals_1_2), .sel(\input [0]), .en(\input [1]));
  Pull_Resistor pull_resistor_1 (.node(outSignals_1_2));
  Multiplexer #(.width(27), .disabled(0)) multiplexer_2 (
    .in0(27'h4060301), .in1(27'h405044), .out(outSignals_3_4_5), .sel(\input [0]), .en(\input [1]));
  Pull_Resistor pull_resistor_2 (.node(outSignals_3_4_5));
endmodule

module DisplayReg1 (
  input  I_Osel,
  input  [3:0] I_Oadr,
  input  in_out,
  input  [3:0] I_Odat,
  output [3:0] out,
  output [3:0] value
);

  wire and_1_out, decoder_1_out0, decoder_1_out1;

  Register #(.width(4)) register_1 (.D(I_Odat), .Q(value), .clk(decoder_1_out0));  // open: en, clr
  assign out = decoder_1_out1 ? value : 4'bz;  // Controlled_Buffer controlled_buffer_1
  and and_1 (and_1_out, ~I_Oadr[3], ~I_Oadr[2], ~I_Oadr[1], I_Oadr[0], I_Osel);  // AND_Gate
  Decoder #(.disabled(0)) decoder_1 (.out0(decoder_1_out0), .out1(decoder_1_out1), .sel(in_out), .en(and_1_out));
endmodule

module DisplayReg2 (
  input  I_Osel,
  input  [3:0] I_Oadr,
  input  in_out,
  input  [3:0] I_Odat,
  output [3:0] out,
  output [3:0] value
);

  wire and_1_out, decoder_1_out0, decoder_1_out1;

  Register #(.width(4)) register_1 (.D(I_Odat), .Q(value), .clk(decoder_1_out0));  // open: en, clr
  assign out = decoder_1_out1 ? value : 4'bz;  // Controlled_Buffer controlled_buffer_1
  and and_1 (and_1_out, ~I_Oadr[3], ~I_Oadr[2], I_Oadr[1], ~I_Oadr[0], I_Osel);  // AND_Gate
  Decoder #(.disabled(0)) decoder_1 (.out0(decoder_1_out0), .out1(decoder_1_out1), .sel(in_out), .en(and_1_out));
endmodule

module DisplayReg3 (
  input  I_Osel,
  input  [3:0] I_Oadr,
  input  in_out,
  input  [3:0] I_Odat,
  output [3:0] out,
  output [3:0] value
);

  wire and_1_out, decoder_1_out0, decoder_1_out1;

  Register #(.width(4)) register_1 (.D(I_Odat), .Q(value), .clk(decoder_1_out0));  // open: en, clr
  assign out = decoder_1_out1 ? value : 4'bz;  // Controlled_Buffer controlled_buffer_1
  and and_1 (and_1_out, ~I_Oadr[3], ~I_Oadr[2], I_Oadr[1], I_Oadr[0], I_Osel);  // AND_Gate
  Decoder #(.disabled(0)) decoder_1 (.out0(decoder_1_out0), .out1(decoder_1_out1), .sel(in_out), .en(and_1_out));
endmodule

module DisplayReg4 (
  input  I_Osel,
  input  [3:0] I_Oadr,
  input  in_out,
  input  [3:0] I_Odat,
  output [3:0] out,
  output [3:0] value
);

  wire and_1_out, decoder_1_out0, decoder_1_out1;

  Register #(.width(4)) register_1 (.D(I_Odat), .Q(value), .clk(decoder_1_out0));  // open: en, clr
  assign out = decoder_1_out1 ? value : 4'bz;  // Controlled_Buffer controlled_buffer_1
  and and_1 (and_1_out, ~I_Oadr[3], I_Oadr[2], ~I_Oadr[1], ~I_Oadr[0], I_Osel);  // AND_Gate
  Decoder #(.disabled(0)) decoder_1 (.out0(decoder_1_out0), .out1(decoder_1_out1), .sel(in_out), .en(and_1_out));
endmodule

module DisplayReg5 (
  input  I_Osel,
  input  [3:0] I_Oadr,
  input  in_out,
  input  [3:0] I_Odat,
  output [3:0] out,
  output [3:0] value
);

  wire and_1_out, decoder_1_out0, decoder_1_out1;

  Register #(.width(4)) register_1 (.D(I_Odat), .Q(value), .clk(decoder_1_out0));  // open: en, clr
  assign out = decoder_1_out1 ? value : 4'bz;  // Controlled_Buffer controlled_buffer_1
  and and_1 (and_1_out, ~I_Oadr[3], I_Oadr[2], ~I_Oadr[1], I_Oadr[0], I_Osel);  // AND_Gate
  Decoder #(.disabled(0)) decoder_1 (.out0(decoder_1_out0), .out1(decoder_1_out1), .sel(in_out), .en(and_1_out));
endmodule

module DisplayReg6 (
  input  I_Osel,
  input  [3:0] I_Oadr,
  input  in_out,
  input  [3:0] I_Odat,
  output [3:0] out,
  output [3:0] value
);

  wire and_1_out, decoder_1_out0, decoder_1_out1;

  Register #(.width(4)) register_1 (.D(I_Odat), .Q(value), .clk(decoder_1_out0));  // open: en, clr
  assign out = decoder_1_out1 ? value : 4'bz;  // Controlled_Buffer controlled_buffer_1
  and and_1 (and_1_out, ~I_Oadr[3], I_Oadr[2], I_Oadr[1], ~I_Oadr[0], I_Osel);  // AND_Gate
  Decoder #(.disabled(0)) decoder_1 (.out0(decoder_1_out0), .out1(decoder_1_out1), .sel(in_out), .en(and_1_out));
endmodule

module DisplayReg7 (
  input  I_Osel,
  input  [3:0] I_Oadr,
  input  in_out,
  input  [3:0] I_Odat,
  output [3:0] out,
  output [3:0] value
);

  wire and_1_out, decoder_1_out0, decoder_1_out1;

  Register #(.width(4)) register_1 (.D(I_Odat), .Q(value), .clk(decoder_1_out0));  // open: en, clr
  assign out = decoder_1_out1 ? value : 4'bz;  // Controlled_Buffer controlled_buffer_1
  and and_1 (and_1_out, ~I_Oadr[3], I_Oadr[2], I_Oadr[1], I_Oadr[0], I_Osel);  // AND_Gate
  Decoder #(.disabled(0)) decoder_1 (.out0(decoder_1_out0), .out1(decoder_1_out1), .sel(in_out), .en(and_1_out));
endmodule

module DisplayReg8 (
  input  I_Osel,
  input  [3:0] I_Oadr,
  input  in_out,
  input  [3:0] I_Odat,
  output [3:0] out,
  output [3:0] value
);

  wire and_1_out, decoder_1_out0, decoder_1_out1;

  Register #(.width(4)) register_1 (.D(I_Odat), .Q(value), .clk(decoder_1_out0));  // open: en, clr
  assign out = decoder_1_out1 ? value : 4'bz;  // Controlled_Buffer controlled_buffer_1
  and and_1 (and_1_out, I_Oadr[3], ~I_Oadr[2], ~I_Oadr[1], ~I_Oadr[0], I_Osel);  // AND_Gate
  Decoder #(.disabled(0)) decoder_1 (.out0(decoder_1_out0), .out1(decoder_1_out1), .sel(in_out), .en(and_1_out));
endmodule

module DisplayReg9 (
  input  I_Osel,
  input  [3:0] I_Oadr,
  input  in_out,
  input  [3:0] I_Odat,
  output [3:0] out,
  output [3:0] value
);

  wire and_1_out, decoder_1_out0, decoder_1_out1;

  Register #(.width(4)) register_1 (.D(I_Odat), .Q(value), .clk(decoder_1_out0));  // open: en, clr
  assign out = decoder_1_out1 ? value : 4'bz;  // Controlled_Buffer controlled_buffer_1
  and and_1 (and_1_out, I_Oadr[3], ~I_Oadr[2], ~I_Oadr[1], I_Oadr[0], I_Osel);  // AND_Gate
  Decoder #(.disabled(0)) decoder_1 (.out0(decoder_1_out0), .out1(decoder_1_out1), .sel(in_out), .en(and_1_out));
endmodule

module PS_saver (
  input  I_O_sel,
  input  [3:0] I_O_Adr,
  input  in_out,
  input  [7:0] I_Odat,
  output [7:0] out
);

  wire and_1_out, decoder_1_out0, decoder_1_out1;
  wire [7:0] register_1_q;

  Register register_1 (.D(I_Odat), .Q(register_1_q), .clk(decoder_1_out0));  // open: en, clr
  assign out = decoder_1_out1 ? register_1_q : 8'bz;  // Controlled_Buffer controlled_buffer_1
  and and_1 (and_1_out, I_O_Adr[3], I_O_Adr[2], I_O_Adr[1], I_O_Adr[0], I_O_sel);
  Decoder #(.disabled(0)) decoder_1 (.out0(decoder_1_out0), .out1(decoder_1_out1), .sel(in_out), .en(and_1_out));
endmodule

module SP_saver (
  input  I_O_sel,
  input  [3:0] I_O_Adr,
  input  in_out,
  input  [7:0] I_Odat,
  output [7:0] out
);

  wire and_1_out, decoder_1_out0, decoder_1_out1;
  wire [7:0] register_1_q;

  Register register_1 (.D(I_Odat), .Q(register_1_q), .clk(decoder_1_out0));  // open: en, clr
  assign out = decoder_1_out1 ? register_1_q : 8'bz;  // Controlled_Buffer controlled_buffer_1
  and and_1 (and_1_out, I_O_Adr[3], I_O_Adr[2], I_O_Adr[1], ~I_O_Adr[0], I_O_sel);  // AND_Gate
  Decoder #(.disabled(0)) decoder_1 (.out0(decoder_1_out0), .out1(decoder_1_out1), .sel(in_out), .en(and_1_out));
endmodule

module Win_loose_screen (
  input  I_O_sel,
  input  [3:0] I_O_Adr,
  input  in_out,
  input  [7:0] I_Odat,
  output player,
  output Draw,
  output computer,
  output [7:0] I_Odat_2
);

  wire and_4_out, decoder_1_out0, decoder_1_out1;
  wire [7:0] register_1_q;

  and and_1 (player, register_1_q[0], register_1_q[1]);
  and and_2 (Draw, register_1_q[0], ~register_1_q[1]);  // AND_Gate
  and and_3 (computer, ~register_1_q[0], register_1_q[1]);  // AND_Gate
  assign I_Odat_2 = decoder_1_out1 ? register_1_q : 8'bz;  // Controlled_Buffer controlled_buffer_1
  Decoder #(.disabled(0)) decoder_1 (.out0(decoder_1_out0), .out1(decoder_1_out1), .sel(in_out), .en(and_4_out));
  Register register_1 (.D(I_Odat), .Q(register_1_q), .clk(decoder_1_out0));  // open: en, clr
  and and_4 (and_4_out, I_O_Adr[3], I_O_Adr[2], ~I_O_Adr[1], ~I_O_Adr[0], I_O_sel);  // AND_Gate

  // Notes on the sheet:
  //   Page number
endmodule

module Move_Selector (
  input  [3:0] S1,
  input  [3:0] S2,
  input  [3:0] S3,
  input  [3:0] S4,
  input  [3:0] S5,
  input  [3:0] S6,
  input  [3:0] S7,
  input  [3:0] S8,
  input  [3:0] S9,
  output [7:0] Move
);

  wire and_5_out, and_6_out, and_7_out, and_16_out, and_17_out, and_18_out, and_25_out, and_26_out,
       and_27_out, S1_0, S1_X, S1_Z, S2_0, S2_X, S2_Z, S3_0, S3_X, S3_Z, S4_0, S4_X, S4_Z, S5_0, S5_X, S5_Z,
       S6_0, S6_X, S6_Z, S7_0, S7_X, S7_Z, S8_0, S8_X, S8_Z, S9_0, S9_X, S9_Z;

  and and_1 (S1_0, S1[1], ~S1[0]);  // AND_Gate
  and and_2 (S1_X, S1[1], S1[0]);
  not not_1 (S1_Z, S1[1]);
  and and_3 (S2_X, S2[1], S2[0]);
  and and_4 (S2_0, S2[1], ~S2[0]);  // AND_Gate
  not not_2 (S2_Z, S2[1]);
  and and_5 (and_5_out, S1_Z, S2_Z, S3_Z, S4_Z, S5_X, S6_Z, S7_Z, S8_Z, S9_Z);
  and and_6 (and_6_out, S1_Z, S2_Z, S3_Z, S4_X, S5_Z, S6_Z, S7_Z, S8_Z, S9_Z);
  and and_7 (and_7_out, S1_Z, S2_Z, S3_Z, S4_Z, S5_Z, S6_Z, S7_X, S8_Z, S9_Z);
  and and_8 (S3_X, S3[1], S3[0]);
  and and_9 (S3_0, S3[1], ~S3[0]);  // AND_Gate
  not not_3 (S3_Z, S3[1]);
  assign Move = and_5_out ? 8'hf1 : 8'bz;  // Controlled_Buffer controlled_buffer_1
  assign Move = and_6_out ? 8'hf5 : 8'bz;  // Controlled_Buffer controlled_buffer_2
  assign Move = and_7_out ? 8'hf5 : 8'bz;  // Controlled_Buffer controlled_buffer_3
  and and_10 (S4_0, S4[1], ~S4[0]);  // AND_Gate
  and and_11 (S4_X, S4[1], S4[0]);
  not not_4 (S4_Z, S4[1]);
  and and_12 (S5_X, S5[1], S5[0]);
  and and_13 (S5_0, S5[1], ~S5[0]);  // AND_Gate
  not not_5 (S5_Z, S5[1]);
  and and_14 (S6_X, S6[1], S6[0]);
  and and_15 (S6_0, S6[1], ~S6[0]);  // AND_Gate
  not not_6 (S6_Z, S6[1]);
  and and_16 (and_16_out, S1_Z, S2_X, S3_Z, S4_Z, S5_Z, S6_Z, S7_Z, S8_Z, S9_Z);
  assign Move = and_16_out ? 8'hf5 : 8'bz;  // Controlled_Buffer controlled_buffer_4
  assign Move = and_17_out ? 8'hf5 : 8'bz;  // Controlled_Buffer controlled_buffer_5
  and and_17 (and_17_out, S1_Z, S2_Z, S3_Z, S4_Z, S5_Z, S6_X, S7_Z, S8_Z, S9_Z);
  and and_18 (and_18_out, S1_Z, S2_Z, S3_Z, S4_Z, S5_Z, S6_Z, S7_Z, S8_Z, S9_X);
  assign Move = and_18_out ? 8'hf5 : 8'bz;  // Controlled_Buffer controlled_buffer_6
  and and_19 (S7_X, S7[1], S7[0]);
  and and_20 (S7_0, S7[1], ~S7[0]);  // AND_Gate
  not not_7 (S7_Z, S7[1]);
  and and_21 (S8_X, S8[1], S8[0]);
  and and_22 (S8_0, S8[1], ~S8[0]);  // AND_Gate
  not not_8 (S8_Z, S8[1]);
  and and_23 (S9_0, S9[1], ~S9[0]);  // AND_Gate
  and and_24 (S9_X, S9[1], S9[0]);
  not not_9 (S9_Z, S9[1]);
  and and_25 (and_25_out, S1_Z, S2_Z, S3_Z, S4_Z, S5_Z, S6_Z, S7_Z, S8_X, S9_Z);
  and and_26 (and_26_out, S1_X, S2_Z, S3_Z, S4_Z, S5_Z, S6_Z, S7_Z, S8_Z, S9_Z);
  and and_27 (and_27_out, S1_Z, S2_Z, S3_X, S4_Z, S5_Z, S6_Z, S7_Z, S8_Z, S9_Z);
  assign Move = and_25_out ? 8'hf5 : 8'bz;  // Controlled_Buffer controlled_buffer_7
  assign Move = and_26_out ? 8'hf5 : 8'bz;  // Controlled_Buffer controlled_buffer_8
  assign Move = and_27_out ? 8'hf5 : 8'bz;  // Controlled_Buffer controlled_buffer_9
  // AND_Gate and_28 has open pins: in0=S1_Z, in1=S2_Z, in2=S3_Z, in3=S4_Z, in4=S5_X, in5=S6_Z, in6=S7_Z, in7=S8_Z, in8=S9_Z, out=open
  // AND_Gate and_29 has open pins: in0=S1_Z, in1=S2_Z, in2=S3_Z, in3=S4_Z, in4=S5_X, in5=S6_Z, in6=S7_Z, in7=S8_Z, in8=S9_Z, out=open

  // Notes on the sheet:
  //   ---
  //   -X-
  //   ---
  //   ---
  //   X--
  //   ---
  //   ---
  //   ---
  //   X--
  //   --X
  //   ---
  //   ---
  //   -X-
  //   ---
  //   ---
  //   ---
  //   --X
  //   ---
  //   ---
  //   ---
  //   --X
  //   ---
  //   ---
  //   X--
  //   ---
  //   ---
  //   -X-
  //   X--
  //   ---
  //   ---
  //   --X
  //   ---
  //   ---
  //   ---
  //   ---
  //   -X-
endmodule
